# Fritzing sketch schematic (saved by Fritzing 0.9.2b)
breadboards: 1

parts:
  R1 = Resistor [tolerance=±5% resistance=1M package=THT]
  R2 = Resistor [tolerance=±5% resistance=220k package=THT]
  R3 = Resistor [tolerance=±5% resistance=1M package=THT]
  C1 = Ceramic Capacitor [capacitance=1µF package="100 mil [THT, multilayer]"]
  Bat = 4 x AAA Battery Mount
  R4 = Resistor [tolerance=±5% resistance=22 package=THT]
  LED1 = LED - 5mm [color="Blue (505nm)" package="5 mm [THT]"]
  R5 = Resistor [tolerance=±5% resistance=22 package=THT]
  LED2 = LED - 5mm [color="Blue (505nm)" package="5 mm [THT]"]

nets:
  N1: R1.Pin_0, Bat.+
  N2: R1.Pin_1, R2.Pin_0, R3.Pin_0
  GND: R2.Pin_1, C1.0, Bat.-, LED1.cathode, LED2.cathode
  ADC: R3.Pin_1, C1.1
  PWM: R4.Pin_0, R5.Pin_0
  N3: R4.Pin_1, LED1.anode
  N4: R5.Pin_1, LED2.anode
